# Fritzing sketch Tetris (saved by Fritzing 0.9.5d)
breadboards: 1

parts:
  R1 = Resistor [tolerance=±5% resistance=1k package=THT]
  R2 = Resistor [tolerance=±5% resistance=1k package=THT]
  R3 = Resistor [tolerance=±5% resistance=1k package=THT]
  R4 = Resistor [tolerance=±5% resistance=1k package=THT]
  R6 = Resistor [tolerance=±5% resistance=1k package=THT]
  S1 = Pushbutton [package="[THT]"]
  S2 = Pushbutton [package="[THT]"]
  S3 = Pushbutton [package="[THT]"]
  S4 = Pushbutton [package="[THT]"]
  S5 = Pushbutton [package="[THT]"]
  S6 = Pushbutton [package="[THT]"]
  R7 = Resistor [tolerance=±5% resistance=1k package=THT]
  Bauteil1 = Arduino Uno (Rev3)

nets:
  N1: R1.Pin_0, S1.Pin_1, S1.Pin_2, Bauteil1.D2
  N2: R1.Pin_1, R2.Pin_1, R3.Pin_1, R4.Pin_1, R6.Pin_1, R7.Pin_1, Bauteil1.GND
  N3: R2.Pin_0, S3.Pin_1, S3.Pin_2, Bauteil1.D7
  N4: R3.Pin_0, S2.Pin_1, S2.Pin_2, Bauteil1.D6_PWM
  N5: R4.Pin_0, S4.Pin_1, S4.Pin_2
  N6: R6.Pin_0, S6.Pin_1, S6.Pin_2, Bauteil1.D3_PWM
  N7: S1.Pin_3, S1.Pin_4, S3.Pin_3, S3.Pin_4, S4.Pin_3, S4.Pin_4, S5.Pin_3, S5.Pin_4, S6.Pin_3, S6.Pin_4, Bauteil1.D5_PWM, Bauteil1.5V
  N8: S2.Pin_3, S2.Pin_4
  N9: S5.Pin_1, S5.Pin_2, R7.Pin_0, Bauteil1.D4

notes:
  Resistors: 1 KΩ
  Buttons:
  TurnLeft MoveLeft Down Drop MoveRight TurnRight
